// Logisim project proj.circ as structural Verilog: 2 circuits, main circuit main
module main (
);

  wire and_1_out, and_2_out, and_3_out, and_4_out, and_5_out, and_6_out, and_7_out, clk, comparator_1_eq,
       comparator_2_eq, comparator_3_eq, comparator_4_eq, d_ff_1_q, debugger_1_p1, iack, irq, kb_clear,
       kb_sel, mem, not_1_out, r_w, ram_sel, ter_clear, ter_sel, tim_sel, word;
  wire [5:0] int_v;
  wire [6:0] kb_sym;
  wire [7:0] kb_control, ter_control, ter_sym;
  wire [15:0] addr, data, debugger_1_p4, debugger_1_p5, fp, pc, ps, r0, r1, r2, r3, r4, r5, r6, sp;

  // Probe on r0
  // Probe on fp
  Clock clock_1 (.out(clk));
  // Probe on r1
  // Probe on r2
  // Probe on sp
  // Probe on pc
  // CdM_16 cdm_16_1: pin names not known; wires that end beside it: irq, int_v, iack, r0, r1, r2, r3, r4, r5, r6, fp, pc, sp, ps, mem, r_w, word, addr
  // Debugger debugger_1: pin names not known; wires that end beside it: debugger_1_p1, 1'b0, clk, debugger_1_p4, debugger_1_p5
  // Probe on r4
  // Probe on r3
  // Probe on ps
  Keyboard keyboard_1 (.clk(clk), .re(kb_control[0]), .clr(kb_clear), .avail(irq), .data(kb_sym));
  Pull_Resistor pull_resistor_1 (.node(kb_control[0]));
  Pull_Resistor pull_resistor_2 (.node(kb_clear));
  // Probe on r5
  // Probe on r6
  assign data = not_1_out ? debugger_1_p4 : 16'bz;  // Controlled_Buffer controlled_buffer_1
  not not_1 (not_1_out, r_w);
  assign debugger_1_p5 = r_w ? data : 16'bz;  // Controlled_Buffer controlled_buffer_2
  // Probe on data
  // Probe on addr
  // Probe on data
  \interconnect  interconnect_1 (.addr(addr), .ram(ram_sel), .kb(kb_sel), .ter(ter_sel), .tim(tim_sel));
  Comparator #(.width(4), .mode("unsigned")) comparator_1 (
    .a(addr[3:0]), .b(4'b0000), .eq(comparator_1_eq));  // open: gt, lt
  Comparator #(.width(4), .mode("unsigned")) comparator_2 (
    .a(addr[3:0]), .b(4'b0010), .eq(comparator_2_eq));  // open: gt, lt
  assign int_v = irq ? 6'b000101 : 6'bz;  // Controlled_Buffer controlled_buffer_3
  and and_1 (and_1_out, comparator_1_eq, kb_sel);
  assign data[7:0] = and_2_out ? {{5{kb_control[7]}}, kb_clear, irq, kb_control[0]} : 8'bz;  // Controlled_Buffer controlled_buffer_4
  assign {{5{kb_control[7]}}, kb_clear, irq, kb_control[0]} = and_3_out ? data[7:0] : 8'bz;  // Controlled_Buffer controlled_buffer_5
  and and_2 (and_2_out, comparator_2_eq, r_w, kb_sel);
  assign data[7:0] = and_1_out ? {1'b0, kb_sym} : 8'bz;  // Controlled_Buffer controlled_buffer_6
  Pull_Resistor pull_resistor_3 (.node(data[15:8]));
  Pull_Resistor pull_resistor_4 (.node(data[15:8]));
  and and_3 (and_3_out, comparator_2_eq, ~r_w, kb_sel);  // AND_Gate
  Pull_Resistor pull_resistor_5 (.node(ter_sym));
  and and_4 (and_4_out, mem, ram_sel);
  TTY tty_1 (.data(ter_sym[6:0]), .clk(clk), .we(d_ff_1_q), .clr(ter_clear));
  D_Flip_Flop d_ff_1 (.clk(clk), .D(ter_control[0]), .Q(d_ff_1_q));  // open: Qn, preset, en, reset
  Pull_Resistor pull_resistor_6 (.node(ter_clear));
  // RAM ram_1: pin names not known; wires that end beside it: debugger_1_p1, addr, word, and_4_out, clk, r_w, data
  Comparator #(.width(4), .mode("unsigned")) comparator_3 (
    .a(addr[3:0]), .b(4'b1000), .eq(comparator_3_eq));  // open: gt, lt
  Comparator #(.width(4), .mode("unsigned")) comparator_4 (
    .a(addr[3:0]), .b(4'b1010), .eq(comparator_4_eq));  // open: gt, lt
  assign ter_sym = and_5_out ? data[7:0] : 8'bz;  // Controlled_Buffer controlled_buffer_7
  and and_5 (and_5_out, comparator_3_eq, ter_sel);
  Pull_Resistor pull_resistor_7 (.node(data[15:8]));
  assign data[7:0] = and_6_out ? {{6{ter_control[7]}}, ter_clear, ter_control[0]} : 8'bz;  // Controlled_Buffer controlled_buffer_8
  Pull_Resistor pull_resistor_8 (.node(data[15:8]));
  assign {{6{ter_control[7]}}, ter_clear, ter_control[0]} = and_7_out ? data[7:0] : 8'bz;  // Controlled_Buffer controlled_buffer_9
  and and_6 (and_6_out, comparator_4_eq, r_w, ter_sel);
  and and_7 (and_7_out, comparator_4_eq, ~r_w, ter_sel);  // AND_Gate
  // also tied to GND on the sheet: {kb_control[7], ter_control[7]}

  // Other names for the same wires on the sheet: kb_next = kb_control[0];
  //   kb_control[6:1] = {{4{kb_control[7]}}, kb_clear, irq}; kb_ready = irq; ter_enable = ter_control[0];
  //   ter_control[6:1] = {{5{ter_control[7]}}, ter_clear}

  // Notes on the sheet:
  //   Подай следующий!
  //   Очисти!
  //   Процессор
  //   Писать сюда :D
  //   Есть символ?
  //   Регистр состояния
  //   Устройства
  //   Клавиатура
  //   Регистр Символа
  //   Генерация Прерывания №5
  //   Отображение на память ;( Я мне кажется переусложнил немнога
  //   read/write регистр
  //   read/write регистр
  //   Память
  //   Терминал
  //   Отображение на память ;(
endmodule

module \interconnect  (
  input  [15:0] addr,
  output ram,
  output kb,
  output ter,
  output tim
);

  wire comparator_2_lt, comparator_3_lt, comparator_4_lt;

  Comparator #(.width(16), .mode("unsigned")) comparator_1 (.a(addr), .b(16'hf000), .lt(ram));  // open: gt, eq
  Comparator #(.width(16), .mode("unsigned")) comparator_2 (
    .a(addr), .b(16'hf008), .lt(comparator_2_lt));  // open: gt, eq
  Comparator #(.width(16), .mode("unsigned")) comparator_3 (
    .a(addr), .b(16'hf00f), .lt(comparator_3_lt));  // open: gt, eq
  Comparator #(.width(16), .mode("unsigned")) comparator_4 (
    .a(addr), .b(16'hf018), .lt(comparator_4_lt));  // open: gt, eq
  and and_1 (kb, ~ram, comparator_2_lt);  // AND_Gate
  and and_2 (ter, ~comparator_2_lt, comparator_3_lt);  // AND_Gate
  and and_3 (tim, ~comparator_3_lt, comparator_4_lt);  // AND_Gate
endmodule
